// Logisim project aiAlu.circ as structural Verilog
module Half_Adder (
  input  a,
  input  b,
  output S,
  output C
);

  xor xor_1 (S, b, a);
  and and_1 (C, b, a);
endmodule

module Full_Adder (
  input  Cin,
  input  a,
  input  b,
  output out_4,
  output out_5
);

  wire and_1_out, and_2_out, and_3_out, xor_1_out;

  xor xor_1 (xor_1_out, a, b);
  and and_1 (and_1_out, Cin, a);
  and and_2 (and_2_out, a, b);
  and and_3 (and_3_out, Cin, b);
  xor xor_2 (out_4, xor_1_out, Cin);
  or or_1 (out_5, and_1_out, and_2_out, and_3_out);
endmodule

module Cpl_2 (
  input  [7:0] in_1,
  output C,
  output [7:0] out_3
);

  wire half_adder_1_c, half_adder_2_c, half_adder_3_c, half_adder_4_c, half_adder_5_c, half_adder_6_c,
       half_adder_8_c;
  wire [7:0] not_1_out;

  assign not_1_out = ~in_1;  // NOT_Gate not_1, 8 bits wide
  Half_Adder half_adder_1 (.S(out_3[0]), .C(half_adder_1_c), .a(1'b1), .b(not_1_out[0]));
  Half_Adder half_adder_2 (.S(out_3[2]), .C(half_adder_2_c), .a(not_1_out[2]), .b(half_adder_3_c));
  Half_Adder half_adder_3 (.S(out_3[1]), .C(half_adder_3_c), .a(not_1_out[1]), .b(half_adder_1_c));
  Half_Adder half_adder_4 (.S(out_3[4]), .C(half_adder_4_c), .a(not_1_out[4]), .b(half_adder_5_c));
  Half_Adder half_adder_5 (.S(out_3[3]), .C(half_adder_5_c), .a(not_1_out[3]), .b(half_adder_2_c));
  Half_Adder half_adder_6 (.S(out_3[5]), .C(half_adder_6_c), .a(not_1_out[5]), .b(half_adder_4_c));
  Half_Adder half_adder_7 (.S(out_3[7]), .C(C), .a(not_1_out[7]), .b(half_adder_8_c));
  Half_Adder half_adder_8 (.S(out_3[6]), .C(half_adder_8_c), .a(not_1_out[6]), .b(half_adder_6_c));
endmodule

module Overflow (
  input  in_1,
  input  in_2,
  input  in_3,
  input  in_4,
  input  in_5,
  input  in_6,
  input  in_7,
  input  in_8,
  input  in_9,
  input  in_10,
  input  in_11,
  input  in_12,
  input  in_13,
  input  in_14,
  input  in_15,
  input  in_16,
  output out_17,
  output out_18,
  output out_19,
  output out_20,
  output out_21,
  output out_22,
  output out_23,
  output out_24,
  output out_25
);

  wire adder_4_bits_2_out_14;

  Adder_4_bits adder_4_bits_1 (
    .in_1(in_7), .in_2(in_8), .in_4(in_5), .in_5(in_6), .in_6(in_3), .in_7(in_4), .in_8(in_1), .in_9(in_2),
    .in_3(adder_4_bits_2_out_14), .out_10(out_21), .out_11(out_20), .out_12(out_19), .out_13(out_18),
    .out_14(out_17));
  Adder_4_bits adder_4_bits_2 (
    .in_1(in_15), .in_2(in_16), .in_4(in_13), .in_5(in_14), .in_6(in_11), .in_7(in_12), .in_8(in_9),
    .in_9(in_10), .in_3(1'b0), .out_10(out_25), .out_11(out_24), .out_12(out_23), .out_13(out_22),
    .out_14(adder_4_bits_2_out_14));
endmodule

module Adder_4_bits (
  input  in_1,
  input  in_2,
  input  in_3,
  input  in_4,
  input  in_5,
  input  in_6,
  input  in_7,
  input  in_8,
  input  in_9,
  output out_10,
  output out_11,
  output out_12,
  output out_13,
  output out_14
);

  wire full_adder_1_out_5, full_adder_2_out_5, full_adder_3_out_5;

  Full_Adder full_adder_1 (.Cin(in_3), .a(in_1), .b(in_2), .out_4(out_10), .out_5(full_adder_1_out_5));
  Full_Adder full_adder_2 (.Cin(full_adder_1_out_5), .a(in_4), .b(in_5), .out_4(out_11), .out_5(full_adder_2_out_5));
  Full_Adder full_adder_3 (.Cin(full_adder_2_out_5), .a(in_6), .b(in_7), .out_4(out_12), .out_5(full_adder_3_out_5));
  Full_Adder full_adder_4 (.Cin(full_adder_3_out_5), .a(in_8), .b(in_9), .out_4(out_13), .out_5(out_14));
endmodule

module and_8_bit (
  input  [7:0] in_1,
  input  [7:0] in_2,
  output [7:0] out_3
);

  assign out_3 = in_1 & in_2;  // AND_Gate and_1, 8 bits wide
endmodule

module not_8_bit (
  input  [7:0] in_1,
  output [7:0] out_2
);

  assign out_2 = ~in_1;  // NOT_Gate not_1, 8 bits wide
endmodule

module or_8_bit (
  input  [7:0] in_1,
  input  [7:0] in_2,
  output [7:0] out_3
);

  assign out_3 = in_1 | in_2;  // OR_Gate or_1, 8 bits wide
endmodule

module ex_or_8_bit (
  input  [7:0] in_1,
  input  [7:0] in_2,
  output [7:0] out_3
);

  assign out_3 = in_1 ^ in_2;  // XOR_Gate xor_1, 8 bits wide
endmodule

module MUX_4_a_1 (
  input  S0,
  input  S1,
  input  in_3,
  input  in_4,
  input  in_5,
  input  in_6,
  output out_7
);

  wire and_1_out, and_2_out, and_3_out, and_4_out, not_1_out, not_2_out;

  not not_1 (not_1_out, S0);
  not not_2 (not_2_out, S1);
  and and_1 (and_1_out, not_2_out, not_1_out, in_3);
  and and_2 (and_2_out, not_1_out, S1, in_4);
  and and_3 (and_3_out, S0, not_2_out, in_5);
  and and_4 (and_4_out, S0, S1, in_6);
  or or_1 (out_7, and_1_out, and_2_out, and_3_out, and_4_out);
endmodule

module MUX_2_a_1 (
  input  in_1,
  input  in_2,
  input  in_3,
  output out_4
);

  wire and_1_out, and_2_out, not_1_out;

  not not_1 (not_1_out, in_1);
  and and_1 (and_1_out, not_1_out, in_2);
  and and_2 (and_2_out, in_1, in_3);
  or or_1 (out_4, and_1_out, and_2_out);
endmodule

module MUX_8_a_1 (
  input  in_1,
  input  in_2,
  input  in_3,
  input  in_4,
  input  in_5,
  input  in_6,
  input  in_7,
  input  in_8,
  input  in_9,
  input  in_10,
  input  in_11,
  output out_12
);

  wire mux_4_a_1_1_out_7, mux_4_a_1_2_out_7;

  MUX_4_a_1 mux_4_a_1_1 (
    .in_3(in_4), .in_4(in_5), .in_5(in_6), .in_6(in_7), .out_7(mux_4_a_1_1_out_7), .S0(in_2), .S1(in_3));
  MUX_4_a_1 mux_4_a_1_2 (
    .in_3(in_8), .in_4(in_9), .in_5(in_10), .in_6(in_11), .out_7(mux_4_a_1_2_out_7), .S0(in_2), .S1(in_3));
  MUX_2_a_1 mux_2_a_1_1 (.in_2(mux_4_a_1_1_out_7), .in_3(mux_4_a_1_2_out_7), .out_4(out_12), .in_1(in_1));
endmodule

module _8_MUX (
  input  in_1,
  input  in_2,
  input  in_3,
  input  in_4,
  input  in_5,
  input  in_6,
  input  in_7,
  input  in_8,
  input  in_9,
  input  in_10,
  input  in_11,
  input  in_12,
  input  in_13,
  input  in_14,
  input  in_15,
  input  in_16,
  input  in_17,
  input  in_18,
  input  in_19,
  input  in_20,
  input  in_21,
  input  in_22,
  input  in_23,
  input  in_24,
  input  in_25,
  input  in_26,
  input  in_27,
  input  in_28,
  input  in_29,
  input  in_30,
  input  in_31,
  input  in_32,
  input  in_33,
  input  in_34,
  input  in_35,
  input  in_36,
  input  in_37,
  input  in_38,
  input  in_39,
  input  in_40,
  input  in_41,
  input  in_42,
  input  in_43,
  input  in_44,
  input  in_45,
  input  in_46,
  input  in_47,
  input  in_48,
  input  in_49,
  input  in_50,
  input  in_51,
  input  in_52,
  input  in_53,
  input  in_54,
  input  in_55,
  input  in_56,
  input  in_57,
  input  in_58,
  input  in_59,
  input  in_60,
  input  in_61,
  input  in_62,
  input  in_63,
  input  in_64,
  input  in_65,
  input  in_66,
  input  in_67,
  output out_68,
  output out_69,
  output out_70,
  output out_71,
  output out_72,
  output out_73,
  output out_74,
  output out_75
);

  MUX_8_a_1 mux_8_a_1_1 (
    .in_4(in_2), .in_5(in_7), .in_6(in_9), .in_7(in_12), .in_8(in_15), .in_9(in_13), .in_10(in_17),
    .in_11(in_19), .out_12(out_69), .in_1(in_4), .in_2(in_5), .in_3(in_6));
  MUX_8_a_1 mux_8_a_1_2 (
    .in_4(in_20), .in_5(in_22), .in_6(in_24), .in_7(in_26), .in_8(in_30), .in_9(in_28), .in_10(in_32),
    .in_11(in_34), .out_12(out_70), .in_1(in_4), .in_2(in_5), .in_3(in_6));
  MUX_8_a_1 mux_8_a_1_3 (
    .in_4(in_37), .in_5(in_39), .in_6(in_41), .in_7(in_43), .in_8(in_47), .in_9(in_45), .in_10(in_49),
    .in_11(in_51), .out_12(out_72), .in_1(in_4), .in_2(in_5), .in_3(in_6));
  MUX_8_a_1 mux_8_a_1_4 (
    .in_4(in_52), .in_5(in_53), .in_6(in_54), .in_7(in_55), .in_8(in_57), .in_9(in_56), .in_10(in_58),
    .in_11(in_59), .out_12(out_74), .in_1(in_4), .in_2(in_5), .in_3(in_6));
  MUX_8_a_1 mux_8_a_1_5 (
    .in_4(in_60), .in_5(in_61), .in_6(in_62), .in_7(in_63), .in_8(in_65), .in_9(in_64), .in_10(in_66),
    .in_11(in_67), .out_12(out_75), .in_1(in_4), .in_2(in_5), .in_3(in_6));
  MUX_8_a_1 mux_8_a_1_6 (
    .in_4(in_1), .in_5(in_3), .in_6(in_8), .in_7(in_10), .in_8(in_14), .in_9(in_11), .in_10(in_16),
    .in_11(in_18), .out_12(out_68), .in_1(in_4), .in_2(in_5), .in_3(in_6));
  MUX_8_a_1 mux_8_a_1_7 (
    .in_4(in_21), .in_5(in_23), .in_6(in_25), .in_7(in_27), .in_8(in_31), .in_9(in_29), .in_10(in_33),
    .in_11(in_35), .out_12(out_71), .in_1(in_4), .in_2(in_5), .in_3(in_6));
  MUX_8_a_1 mux_8_a_1_8 (
    .in_4(in_36), .in_5(in_38), .in_6(in_40), .in_7(in_42), .in_8(in_46), .in_9(in_44), .in_10(in_48),
    .in_11(in_50), .out_12(out_73), .in_1(in_4), .in_2(in_5), .in_3(in_6));

  // Other names for the same wires on the sheet: S0 = in_6; S1 = in_5; S2 = in_4
endmodule

module MUX_FINALE (
  input  in_1,
  input  in_2,
  input  in_3,
  input  [7:0] in_4,
  input  [7:0] in_5,
  input  [7:0] in_6,
  input  [7:0] in_7,
  input  [7:0] in_8,
  input  [7:0] in_9,
  input  [7:0] in_10,
  input  [7:0] in_11,
  output [7:0] out_12
);

  _8_MUX u_8_mux_1 (
    .in_1(in_4[5]), .in_2(in_4[0]), .in_3(in_5[5]), .in_7(in_5[0]), .in_8(in_6[5]), .in_9(in_6[0]),
    .in_10(in_7[5]), .in_11(in_8[5]), .in_12(in_7[0]), .in_13(in_8[0]), .in_14(in_9[5]), .in_15(in_9[0]),
    .in_16(in_10[5]), .in_17(in_10[0]), .in_18(in_11[5]), .in_19(in_11[0]), .in_20(in_4[1]), .in_21(in_4[6]),
    .in_22(in_5[1]), .in_23(in_5[6]), .in_24(in_6[1]), .in_25(in_6[6]), .in_26(in_7[1]), .in_27(in_7[6]),
    .in_28(in_8[1]), .in_29(in_8[6]), .in_30(in_9[1]), .in_31(in_9[6]), .in_32(in_10[1]), .in_33(in_10[6]),
    .in_34(in_11[1]), .in_35(in_11[6]), .in_36(in_4[7]), .in_37(in_4[2]), .in_38(in_5[7]), .in_39(in_5[2]),
    .in_40(in_6[7]), .in_41(in_6[2]), .in_42(in_7[7]), .in_43(in_7[2]), .in_44(in_8[7]), .in_45(in_8[2]),
    .in_46(in_9[7]), .in_47(in_9[2]), .in_48(in_10[7]), .in_49(in_10[2]), .in_50(in_11[7]), .in_51(in_11[2]),
    .in_52(in_4[3]), .in_53(in_5[3]), .in_54(in_6[3]), .in_55(in_7[3]), .in_56(in_8[3]), .in_57(in_9[3]),
    .in_58(in_10[3]), .in_59(in_11[3]), .in_60(in_4[4]), .in_61(in_5[4]), .in_62(in_6[4]), .in_63(in_7[4]),
    .in_64(in_8[4]), .in_65(in_9[4]), .in_66(in_10[4]), .in_67(in_11[4]), .out_68(out_12[5]),
    .out_69(out_12[0]), .out_70(out_12[1]), .out_71(out_12[6]), .out_72(out_12[2]), .out_73(out_12[7]),
    .out_74(out_12[4]), .out_75(out_12[3]), .in_4(in_1), .in_5(in_2), .in_6(in_3));
endmodule

module BULABULABULA (
  input  [7:0] in_1,
  input  [7:0] in_2,
  output out_3
);

  wire [7:0] shalabalabala_1_out_3;

  SHALABALABALA shalabalabala_1 (.in_1(in_2), .in_2(in_1), .out_3(shalabalabala_1_out_3), .out_4(out_3));
  MUX_FINALE mux_finale_1 (.in_4(shalabalabala_1_out_3));  // open: in_5, in_6, in_7, in_8, in_9, in_10, in_11, out_12, in_1, in_2, in_3

  // Other names for the same wires on the sheet: A[7:0] = in_1; B[7:0] = in_2
endmodule

module SHALABALABALA (
  input  [7:0] in_1,
  input  [7:0] in_2,
  output [7:0] out_3,
  output out_4
);

  Overflow overflow_1 (
    .in_1(in_2[0]), .in_3(in_2[1]), .in_5(in_2[2]), .in_7(in_2[3]), .in_9(in_2[4]), .in_11(in_2[5]),
    .in_13(in_2[6]), .in_15(in_2[7]), .out_17(out_4), .in_2(in_1[0]), .in_4(in_1[1]), .in_6(in_1[2]),
    .in_8(in_1[3]), .in_10(in_1[4]), .in_12(in_1[5]), .in_14(in_1[6]), .in_16(in_1[7]), .out_18(out_3[0]),
    .out_19(out_3[1]), .out_20(out_3[2]), .out_21(out_3[3]), .out_22(out_3[4]), .out_23(out_3[5]),
    .out_24(out_3[6]), .out_25(out_3[7]));
endmodule

module SOTTRATTORE (
  input  [7:0] in_1,
  input  [7:0] in_2,
  output out_3,
  output [7:0] out_4,
  output out_5
);

  wire [7:0] cpl_2_1_out_3;

  Cpl_2 cpl_2_1 (.in_1(in_2), .C(out_3), .out_3(cpl_2_1_out_3));
  Overflow overflow_1 (
    .in_1(in_1[0]), .in_3(in_1[1]), .in_5(in_1[2]), .in_7(in_1[3]), .in_9(in_1[4]), .in_11(in_1[5]),
    .in_13(in_1[6]), .in_15(in_1[7]), .out_17(out_5), .in_2(cpl_2_1_out_3[0]), .in_4(cpl_2_1_out_3[1]),
    .in_6(cpl_2_1_out_3[2]), .in_8(cpl_2_1_out_3[3]), .in_10(cpl_2_1_out_3[4]), .in_12(cpl_2_1_out_3[5]),
    .in_14(cpl_2_1_out_3[6]), .in_16(cpl_2_1_out_3[7]), .out_18(out_4[0]), .out_19(out_4[1]),
    .out_20(out_4[2]), .out_21(out_4[3]), .out_22(out_4[4]), .out_23(out_4[5]), .out_24(out_4[6]),
    .out_25(out_4[7]));
endmodule
